// Logisim project RV.circ as structural Verilog
module EXE_ALU_BarrelShifter (
  input  CLKi,
  input  RIGHTi,
  input  [4:0] SHAMTi,
  input  [31:0] D,
  input  ARITHi
);

  wire exe_alu_barrelshifter_stage1_1_righto, exe_alu_barrelshifter_stage1_1_signo;
  wire [3:0] exe_alu_barrelshifter_stage1_1_shamto;
  wire [31:0] exe_alu_barrelshifter_stage1_1_q;

  EXE_ALU_BarrelShifter_Stage1 exe_alu_barrelshifter_stage1_1 (
    .RIGHTi(RIGHTi), .SHAMTi(SHAMTi), .D(D), .ARITHi(ARITHi), .RIGHTo(exe_alu_barrelshifter_stage1_1_righto),
    .SHAMTo(exe_alu_barrelshifter_stage1_1_shamto), .Q(exe_alu_barrelshifter_stage1_1_q),
    .SIGNo(exe_alu_barrelshifter_stage1_1_signo));
  Register #(.width(1)) register_1 (
    .D(exe_alu_barrelshifter_stage1_1_righto), .en(1'b1), .clk(CLKi), .clr(1'b0));  // open: Q
  Register #(.width(4)) register_2 (
    .D(exe_alu_barrelshifter_stage1_1_shamto), .en(1'b1), .clk(CLKi), .clr(1'b0));  // open: Q
  Register #(.width(32)) register_3 (
    .D(exe_alu_barrelshifter_stage1_1_q), .en(1'b1), .clk(CLKi), .clr(1'b0));  // open: Q
  Register #(.width(1)) register_4 (
    .D(exe_alu_barrelshifter_stage1_1_signo), .en(1'b1), .clk(CLKi), .clr(1'b0));  // open: Q
endmodule

module EXE_ALU_BarrelShifter_Stage1 (
  input  RIGHTi,
  input  [4:0] SHAMTi,
  input  [31:0] D,
  input  ARITHi,
  output RIGHTo,
  output [3:0] SHAMTo,
  output [31:0] Q,
  output SIGNo
);

  and and_1 (SIGNo, D[31], ARITHi);
  Multiplexer #(.select(2)) multiplexer_1 (
    .in0(D[0]), .in1(D[0]), .in2(1'b0), .in3(D[16]), .out(Q[0]), .sel({SHAMTi[4], RIGHTi}));
  Multiplexer #(.select(2)) multiplexer_2 (
    .in0(D[1]), .in1(D[1]), .in2(1'b0), .in3(D[17]), .out(Q[1]), .sel({SHAMTi[4], RIGHTi}));
  Multiplexer #(.select(2)) multiplexer_3 (
    .in0(D[2]), .in1(D[2]), .in2(1'b0), .in3(D[18]), .out(Q[2]), .sel({SHAMTi[4], RIGHTi}));
  Multiplexer #(.select(2)) multiplexer_4 (
    .in0(D[3]), .in1(D[3]), .in2(1'b0), .in3(D[19]), .out(Q[3]), .sel({SHAMTi[4], RIGHTi}));
  Multiplexer #(.select(2)) multiplexer_5 (
    .in0(D[4]), .in1(D[4]), .in2(1'b0), .in3(D[20]), .out(Q[4]), .sel({SHAMTi[4], RIGHTi}));
  Multiplexer #(.select(2)) multiplexer_6 (
    .in0(D[5]), .in1(D[5]), .in2(1'b0), .in3(D[21]), .out(Q[5]), .sel({SHAMTi[4], RIGHTi}));
  Multiplexer #(.select(2)) multiplexer_7 (
    .in0(D[6]), .in1(D[6]), .in2(1'b0), .in3(D[22]), .out(Q[6]), .sel({SHAMTi[4], RIGHTi}));
  Multiplexer #(.select(2)) multiplexer_8 (
    .in0(D[7]), .in1(D[7]), .in2(1'b0), .in3(D[23]), .out(Q[7]), .sel({SHAMTi[4], RIGHTi}));
  Multiplexer #(.select(2)) multiplexer_9 (
    .in0(D[8]), .in1(D[8]), .in2(1'b0), .in3(D[24]), .out(Q[8]), .sel({SHAMTi[4], RIGHTi}));
  Multiplexer #(.select(2)) multiplexer_10 (
    .in0(D[9]), .in1(D[9]), .in2(1'b0), .in3(D[25]), .out(Q[9]), .sel({SHAMTi[4], RIGHTi}));
  Multiplexer #(.select(2)) multiplexer_11 (
    .in0(D[10]), .in1(D[10]), .in2(1'b0), .in3(D[26]), .out(Q[10]), .sel({SHAMTi[4], RIGHTi}));
  Multiplexer #(.select(2)) multiplexer_12 (
    .in0(D[11]), .in1(D[11]), .in2(1'b0), .in3(D[27]), .out(Q[11]), .sel({SHAMTi[4], RIGHTi}));
  Multiplexer #(.select(2)) multiplexer_13 (
    .in0(D[12]), .in1(D[12]), .in2(1'b0), .in3(D[28]), .out(Q[12]), .sel({SHAMTi[4], RIGHTi}));
  Multiplexer #(.select(2)) multiplexer_14 (
    .in0(D[13]), .in1(D[13]), .in2(1'b0), .in3(D[29]), .out(Q[13]), .sel({SHAMTi[4], RIGHTi}));
  Multiplexer #(.select(2)) multiplexer_15 (
    .in0(D[14]), .in1(D[14]), .in2(1'b0), .in3(D[30]), .out(Q[14]), .sel({SHAMTi[4], RIGHTi}));
  Multiplexer #(.select(2)) multiplexer_16 (
    .in0(D[15]), .in1(D[15]), .in2(1'b0), .in3(D[31]), .out(Q[15]), .sel({SHAMTi[4], RIGHTi}));
  Multiplexer #(.select(2)) multiplexer_17 (
    .in0(D[16]), .in1(D[16]), .in2(D[0]), .in3(SIGNo), .out(Q[16]), .sel({SHAMTi[4], RIGHTi}));
  Multiplexer #(.select(2)) multiplexer_18 (
    .in0(D[17]), .in1(D[17]), .in2(D[1]), .in3(SIGNo), .out(Q[17]), .sel({SHAMTi[4], RIGHTi}));
  Multiplexer #(.select(2)) multiplexer_19 (
    .in0(D[18]), .in1(D[18]), .in2(D[2]), .in3(SIGNo), .out(Q[18]), .sel({SHAMTi[4], RIGHTi}));
  Multiplexer #(.select(2)) multiplexer_20 (
    .in0(D[19]), .in1(D[19]), .in2(D[3]), .in3(SIGNo), .out(Q[19]), .sel({SHAMTi[4], RIGHTi}));
  Multiplexer #(.select(2)) multiplexer_21 (
    .in0(D[20]), .in1(D[20]), .in2(D[4]), .in3(SIGNo), .out(Q[20]), .sel({SHAMTi[4], RIGHTi}));
  Multiplexer #(.select(2)) multiplexer_22 (
    .in0(D[21]), .in1(D[21]), .in2(D[5]), .in3(SIGNo), .out(Q[21]), .sel({SHAMTi[4], RIGHTi}));
  Multiplexer #(.select(2)) multiplexer_23 (
    .in0(D[22]), .in1(D[22]), .in2(D[6]), .in3(SIGNo), .out(Q[22]), .sel({SHAMTi[4], RIGHTi}));
  Multiplexer #(.select(2)) multiplexer_24 (
    .in0(D[23]), .in1(D[23]), .in2(D[7]), .in3(SIGNo), .out(Q[23]), .sel({SHAMTi[4], RIGHTi}));
  Multiplexer #(.select(2)) multiplexer_25 (
    .in0(D[24]), .in1(D[24]), .in2(D[8]), .in3(SIGNo), .out(Q[24]), .sel({SHAMTi[4], RIGHTi}));
  Multiplexer #(.select(2)) multiplexer_26 (
    .in0(D[25]), .in1(D[25]), .in2(D[9]), .in3(SIGNo), .out(Q[25]), .sel({SHAMTi[4], RIGHTi}));
  Multiplexer #(.select(2)) multiplexer_27 (
    .in0(D[26]), .in1(D[26]), .in2(D[10]), .in3(SIGNo), .out(Q[26]), .sel({SHAMTi[4], RIGHTi}));
  Multiplexer #(.select(2)) multiplexer_28 (
    .in0(D[27]), .in1(D[27]), .in2(D[11]), .in3(SIGNo), .out(Q[27]), .sel({SHAMTi[4], RIGHTi}));
  Multiplexer #(.select(2)) multiplexer_29 (
    .in0(D[28]), .in1(D[28]), .in2(D[12]), .in3(SIGNo), .out(Q[28]), .sel({SHAMTi[4], RIGHTi}));
  Multiplexer #(.select(2)) multiplexer_30 (
    .in0(D[29]), .in1(D[29]), .in2(D[13]), .in3(SIGNo), .out(Q[29]), .sel({SHAMTi[4], RIGHTi}));
  Multiplexer #(.select(2)) multiplexer_31 (
    .in0(D[30]), .in1(D[30]), .in2(D[14]), .in3(SIGNo), .out(Q[30]), .sel({SHAMTi[4], RIGHTi}));
  Multiplexer #(.select(2)) multiplexer_32 (
    .in0(D[31]), .in1(D[31]), .in2(D[15]), .in3(SIGNo), .out(Q[31]), .sel({SHAMTi[4], RIGHTi}));

  assign RIGHTo = RIGHTi;
  assign SHAMTo = SHAMTi[3:0];
endmodule
